// Logisim project laberinto.circ as structural Verilog: 9 circuits, main circuit main
module main (
  input  [2:0] X,
  input  [2:0] Y,
  input  in_3
);

  wire clock_1_out, ff_d_1_a, ff_d_1_b, ff_d_1_c, ff_d_1_d, ff_d_1_e;
  wire [2:0] logica_de_estados_1_x, logica_de_estados_1_y, logica_de_salida_1_x, logica_de_salida_1_y;
  wire [3:0] ff_d_1_direccion_2, logica_de_estados_1_direccion, logica_de_salida_1_direccion_2;
  wire [4:0] ff_d_1_out_7, logica_de_estados_1_estado;

  // Probe on logica_de_estados_1_x
  Logica_de_Estados logica_de_estados_1 (
    .X0(X[2]), .X1(X[1]), .X2(X[0]), .Y0(Y[2]), .Y1(Y[1]), .Y2(Y[0]), .A(ff_d_1_a), .B(ff_d_1_b),
    .C(ff_d_1_c), .D(ff_d_1_d), .E(ff_d_1_e), .ESTADO(logica_de_estados_1_estado), .X(logica_de_estados_1_x),
    .Y(logica_de_estados_1_y), .DIRECCION(logica_de_estados_1_direccion), .S(in_3));
  // Probe on logica_de_estados_1_y
  Clock clock_1 (.out(clock_1_out));
  FF_D ff_d_1 (
    .ESTADO(logica_de_estados_1_estado), .out_7(ff_d_1_out_7), .DIRECCION(logica_de_estados_1_direccion),
    .DIRECCION_2(ff_d_1_direccion_2), .in_2(clock_1_out), .A(ff_d_1_a), .B(ff_d_1_b), .C(ff_d_1_c),
    .D(ff_d_1_d), .E(ff_d_1_e));
  // Probe on logica_de_salida_1_x
  Logica_de_Salida logica_de_salida_1 (
    .ESTADO(ff_d_1_out_7), .X(logica_de_salida_1_x), .Y(logica_de_salida_1_y),
    .DIRECCION_2(logica_de_salida_1_direccion_2), .DIRECCION(ff_d_1_direccion_2));
  // Probe on logica_de_salida_1_y
  // Probe on logica_de_salida_1_direccion_2

  // Notes on the sheet:
  //   Posicion Actual
  //   CLK
  //   Posicion Siguiente
  //   Direccion
endmodule

module Logica_de_Estados (
  input  X0,
  input  X1,
  input  X2,
  input  Y0,
  input  Y1,
  input  Y2,
  input  A,
  input  B,
  input  C,
  input  D,
  input  E,
  input  S,
  output [2:0] X,
  output [3:0] DIRECCION,
  output [2:0] Y,
  output [4:0] ESTADO
);

  wire [4:0] pos_estado_1_s4;

  POS___ESTADO pos_estado_1 (
    .A1(X0), .A2(X1), .A3(X2), .B1(Y0), .B2(Y1), .B3(Y2), .S0(pos_estado_1_s4[4]), .S1(pos_estado_1_s4[3]),
    .S2(pos_estado_1_s4[2]), .S3(pos_estado_1_s4[1]), .S4(pos_estado_1_s4[0]));
  Multiplexer #(.width(5), .enable("false")) multiplexer_1 (
    .in0(pos_estado_1_s4), .in1({A, B, C, D, E}), .out(ESTADO), .sel(S));
  ESTADO___POS estado_pos_1 (
    .S0(ESTADO[4]), .S1(ESTADO[3]), .S2(ESTADO[2]), .S3(ESTADO[1]), .S4(ESTADO[0]), .A1(X[2]), .A2(X[1]),
    .A3(X[0]), .B1(Y[2]), .B2(Y[1]), .B3(Y[0]));
  Movimientos movimientos_1 (
    .A1(X[2]), .A2(X[1]), .A3(X[0]), .B1(Y[2]), .B2(Y[1]), .B3(Y[0]), .S1(DIRECCION[3]), .S2(DIRECCION[2]),
    .S3(DIRECCION[1]), .S4(DIRECCION[0]));
endmodule

module FF_D (
  input  [3:0] DIRECCION,
  input  in_2,
  input  [4:0] ESTADO,
  output [3:0] DIRECCION_2,
  output A,
  output B,
  output [4:0] out_7,
  output C,
  output D,
  output E
);

  FlipFlop_D flipflop_d_1 (.CLK(in_2), .D(out_7[4]), .A(A), .RESET(1'b1));  // open: NOT_A
  FlipFlop_D flipflop_d_2 (.CLK(in_2), .D(out_7[3]), .A(B), .RESET(1'b1));  // open: NOT_A
  FlipFlop_D flipflop_d_3 (.CLK(in_2), .D(out_7[2]), .A(C), .RESET(1'b1));  // open: NOT_A
  FlipFlop_D flipflop_d_4 (.CLK(in_2), .D(out_7[1]), .A(D), .RESET(1'b1));  // open: NOT_A
  FlipFlop_D flipflop_d_5 (.CLK(in_2), .D(out_7[0]), .A(E), .RESET(1'b1));  // open: NOT_A
  Mejor_movimiento mejor_movimiento_1 (
    .A(ESTADO[4]), .B(ESTADO[3]), .C(ESTADO[2]), .D(ESTADO[1]), .E(ESTADO[0]), .A1(out_7[4]), .B1(out_7[3]),
    .C1(out_7[2]), .D1(out_7[1]), .E1(out_7[0]));

  assign DIRECCION_2 = DIRECCION;
endmodule

module Logica_de_Salida (
  input  [4:0] ESTADO,
  input  [3:0] DIRECCION,
  output [2:0] X,
  output [2:0] Y,
  output [3:0] DIRECCION_2
);

  ESTADO___POS estado_pos_1 (
    .S0(ESTADO[4]), .S1(ESTADO[3]), .S2(ESTADO[2]), .S3(ESTADO[1]), .S4(ESTADO[0]), .A1(X[2]), .A2(X[1]),
    .A3(X[0]), .B1(Y[2]), .B2(Y[1]), .B3(Y[0]));

  assign DIRECCION_2 = DIRECCION;
endmodule

module Movimientos (
  input  A1,
  input  A2,
  input  A3,
  input  B1,
  input  B2,
  input  B3,
  output S1,
  output S2,
  output S3,
  output S4
);

  wire and_1_out, and_2_out, and_3_out, and_4_out, and_5_out, and_6_out, and_7_out, and_8_out, and_9_out,
       and_10_out, and_11_out, and_12_out, and_13_out, and_14_out, and_15_out, and_16_out, and_17_out,
       and_18_out, and_19_out, and_20_out, and_21_out, and_22_out, and_23_out, not_1_out, not_2_out,
       not_3_out, not_4_out, not_5_out, not_6_out, not_7_out, not_8_out, not_9_out, not_10_out, not_11_out,
       not_12_out, not_13_out, not_14_out, not_15_out, not_16_out, not_17_out, not_18_out, not_19_out,
       not_20_out, not_21_out, not_22_out, not_23_out, not_24_out, not_25_out, not_26_out, not_27_out,
       not_28_out, not_29_out, not_30_out, not_31_out, not_32_out, not_33_out, not_34_out, not_35_out,
       not_36_out, not_37_out, not_38_out, not_39_out, not_40_out, not_41_out, not_42_out, not_43_out,
       not_44_out, not_45_out, not_46_out, not_47_out, not_48_out, not_49_out, not_50_out, not_51_out,
       not_52_out;

  not not_1 (not_1_out, A2);
  not not_2 (not_2_out, A3);
  not not_3 (not_3_out, B1);
  not not_4 (not_4_out, B1);
  not not_5 (not_5_out, B3);
  not not_6 (not_6_out, B1);
  not not_7 (not_7_out, B3);
  not not_8 (not_8_out, B2);
  not not_9 (not_9_out, B3);
  not not_10 (not_10_out, A1);
  not not_11 (not_11_out, A2);
  not not_12 (not_12_out, B1);
  not not_13 (not_13_out, B3);
  not not_14 (not_14_out, A1);
  not not_15 (not_15_out, A3);
  not not_16 (not_16_out, A3);
  not not_17 (not_17_out, B2);
  not not_18 (not_18_out, A2);
  not not_19 (not_19_out, A3);
  not not_20 (not_20_out, B2);
  not not_21 (not_21_out, B3);
  not not_22 (not_22_out, A1);
  not not_23 (not_23_out, B1);
  not not_24 (not_24_out, A2);
  not not_25 (not_25_out, A3);
  not not_26 (not_26_out, B1);
  not not_27 (not_27_out, B2);
  not not_28 (not_28_out, A2);
  not not_29 (not_29_out, A3);
  not not_30 (not_30_out, B1);
  not not_31 (not_31_out, B3);
  not not_32 (not_32_out, A2);
  not not_33 (not_33_out, A3);
  not not_34 (not_34_out, B2);
  not not_35 (not_35_out, B3);
  not not_36 (not_36_out, B1);
  not not_37 (not_37_out, B2);
  not not_38 (not_38_out, B3);
  not not_39 (not_39_out, A1);
  not not_40 (not_40_out, B1);
  not not_41 (not_41_out, B2);
  not not_42 (not_42_out, A1);
  not not_43 (not_43_out, A2);
  not not_44 (not_44_out, A1);
  not not_45 (not_45_out, B1);
  not not_46 (not_46_out, B2);
  not not_47 (not_47_out, A1);
  not not_48 (not_48_out, B3);
  not not_49 (not_49_out, B2);
  not not_50 (not_50_out, B3);
  not not_51 (not_51_out, A2);
  not not_52 (not_52_out, B2);
  and and_1 (and_1_out, A1, not_1_out, not_2_out, not_3_out, B2, B3);
  and and_2 (and_2_out, A1, A3, not_4_out, B2, not_5_out);
  and and_3 (and_3_out, A1, A3, B1, B2, B3);
  and and_4 (and_4_out, A1, A2, not_6_out, B2, not_7_out);
  and and_5 (and_5_out, A1, A2, B1, B2, B3);
  and and_6 (and_6_out, A1, A2, A3, B1, not_8_out, not_9_out);
  and and_7 (and_7_out, not_10_out, not_11_out, A3, not_12_out, B2, not_13_out);
  and and_8 (and_8_out, not_14_out, A2, not_15_out, B1, B3);
  and and_9 (and_9_out, A2, not_16_out, B1, not_17_out, B3);
  and and_10 (and_10_out, A1, not_18_out, not_19_out, B1, B2);
  and and_11 (and_11_out, A1, A2, A3, B1, not_20_out, not_21_out);
  and and_12 (and_12_out, not_22_out, A2, A3, not_23_out, B2, B3);
  and and_13 (and_13_out, A1, not_24_out, not_25_out, not_26_out, not_27_out, B3);
  and and_14 (and_14_out, A1, not_28_out, not_29_out, not_30_out, B2, not_31_out);
  and and_15 (and_15_out, A1, not_32_out, not_33_out, B1, not_34_out, not_35_out);
  and and_16 (and_16_out, A1, A2, A3, not_36_out, not_37_out, B3);
  and and_17 (and_17_out, A1, A2, A3, B1, not_38_out);
  and and_18 (and_18_out, not_39_out, A3, not_40_out, not_41_out, B3);
  and and_19 (and_19_out, not_42_out, not_43_out, A3, B1, B2, B3);
  and and_20 (and_20_out, not_44_out, A2, not_45_out, not_46_out, B3);
  and and_21 (and_21_out, not_47_out, A2, B1, not_48_out);
  and and_22 (and_22_out, A2, B1, not_49_out, not_50_out);
  and and_23 (and_23_out, A1, not_51_out, B1, not_52_out, B3);
  or or_1 (S1, and_1_out, and_2_out, and_3_out, and_4_out, and_5_out, and_6_out);
  or or_2 (S2, and_7_out, and_8_out, and_9_out, and_10_out, and_11_out);
  or or_3 (S3, and_12_out, and_13_out, and_14_out, and_15_out, and_16_out, and_17_out);
  or or_4 (S4, and_18_out, and_19_out, and_20_out, and_21_out, and_22_out, and_23_out);
endmodule

module POS___ESTADO (
  input  A1,
  input  A2,
  input  A3,
  input  B1,
  input  B2,
  input  B3,
  output S0,
  output S1,
  output S2,
  output S3,
  output S4
);

  wire and_1_out, and_2_out, and_3_out, and_4_out, and_5_out, and_6_out, and_7_out, and_8_out, and_9_out,
       and_10_out, and_11_out, and_12_out, and_13_out, and_14_out, and_15_out, and_16_out, and_17_out,
       and_18_out, and_19_out, and_20_out, and_21_out, and_22_out, and_23_out, and_24_out, and_25_out,
       and_26_out, not_1_out, not_2_out, not_3_out, not_4_out, not_5_out, not_6_out, not_7_out, not_8_out,
       not_9_out, not_10_out, not_11_out, not_12_out, not_13_out, not_14_out, not_15_out, not_16_out,
       not_17_out, not_18_out, not_19_out, not_20_out, not_21_out, not_22_out, not_23_out, not_24_out,
       not_25_out, not_26_out, not_27_out, not_28_out, not_29_out, not_30_out, not_31_out, not_32_out,
       not_33_out, not_34_out, not_35_out, not_36_out, not_37_out, not_38_out, not_39_out;

  not not_1 (not_1_out, A2);
  not not_2 (not_2_out, A2);
  not not_3 (not_3_out, B2);
  not not_4 (not_4_out, B3);
  not not_5 (not_5_out, A1);
  not not_6 (not_6_out, B2);
  not not_7 (not_7_out, B1);
  not not_8 (not_8_out, A2);
  not not_9 (not_9_out, A3);
  not not_10 (not_10_out, B1);
  not not_11 (not_11_out, B2);
  not not_12 (not_12_out, A3);
  not not_13 (not_13_out, B3);
  not not_14 (not_14_out, A1);
  not not_15 (not_15_out, B2);
  not not_16 (not_16_out, A2);
  not not_17 (not_17_out, B3);
  not not_18 (not_18_out, A3);
  not not_19 (not_19_out, A1);
  not not_20 (not_20_out, B1);
  not not_21 (not_21_out, A3);
  not not_22 (not_22_out, B1);
  not not_23 (not_23_out, A3);
  not not_24 (not_24_out, B2);
  not not_25 (not_25_out, B3);
  not not_26 (not_26_out, A3);
  not not_27 (not_27_out, B2);
  not not_28 (not_28_out, B3);
  not not_29 (not_29_out, A2);
  not not_30 (not_30_out, A2);
  not not_31 (not_31_out, B1);
  not not_32 (not_32_out, A3);
  not not_33 (not_33_out, B3);
  not not_34 (not_34_out, A1);
  not not_35 (not_35_out, B2);
  not not_36 (not_36_out, A1);
  not not_37 (not_37_out, B2);
  not not_38 (not_38_out, A3);
  not not_39 (not_39_out, B3);
  and and_1 (and_1_out, not_1_out, B1, B3);
  and and_2 (and_2_out, B1, B2);
  and and_3 (and_3_out, A1, A2, B1);
  and and_4 (and_4_out, not_2_out, not_3_out, not_4_out);
  and and_5 (and_5_out, B2, B3);
  and and_6 (and_6_out, not_5_out, B1, not_6_out);
  and and_7 (and_7_out, A1, A3, B1, B2);
  and and_8 (and_8_out, A1, A2, A3, not_7_out);
  and and_9 (and_9_out, not_8_out, not_9_out, not_10_out, not_11_out);
  and and_10 (and_10_out, not_12_out, B2, not_13_out);
  and and_11 (and_11_out, not_14_out, B1, not_15_out);
  and and_12 (and_12_out, A2, A3, B1);
  and and_13 (and_13_out, A1, not_16_out, not_17_out);
  and and_14 (and_14_out, A1, A2, not_18_out, B2);
  and and_15 (and_15_out, not_19_out, A2, not_20_out);
  and and_16 (and_16_out, A2, not_21_out, not_22_out);
  and and_17 (and_17_out, A2, not_23_out, not_24_out, B3);
  and and_18 (and_18_out, A2, B1, B2, not_25_out);
  and and_19 (and_19_out, A1, not_26_out, not_27_out, not_28_out);
  and and_20 (and_20_out, A1, not_29_out, B2, B3);
  and and_21 (and_21_out, A1, not_30_out, A3, not_31_out);
  and and_22 (and_22_out, not_32_out, B2, not_33_out);
  and and_23 (and_23_out, not_34_out, B1, not_35_out, B3);
  and and_24 (and_24_out, not_36_out, A3, not_37_out);
  and and_25 (and_25_out, A3, B3);
  and and_26 (and_26_out, A1, A2, not_38_out, not_39_out);
  or or_1 (S0, and_1_out, and_2_out, and_3_out);
  or or_2 (S1, and_4_out, and_5_out, and_6_out, and_7_out, and_8_out);
  or or_3 (S2, and_9_out, and_10_out, and_11_out, and_12_out, and_13_out, and_14_out);
  or or_4 (S3, and_15_out, and_16_out, and_17_out, and_18_out, and_19_out, and_20_out, and_21_out);
  or or_5 (S4, and_22_out, and_23_out, and_24_out, and_25_out, and_26_out);
endmodule

module ESTADO___POS (
  input  S0,
  input  S1,
  input  S2,
  input  S3,
  input  S4,
  output A1,
  output A2,
  output A3,
  output B1,
  output B2,
  output B3
);

  wire and_1_out, and_2_out, and_3_out, and_4_out, and_5_out, and_6_out, and_7_out, and_8_out, and_9_out,
       and_10_out, and_11_out, and_12_out, and_13_out, and_14_out, and_15_out, and_16_out, and_17_out,
       and_18_out, and_19_out, and_20_out, and_21_out, and_22_out, and_23_out, and_24_out, and_25_out,
       and_26_out, and_27_out, and_28_out, and_29_out, and_30_out, and_31_out, and_32_out, and_33_out,
       and_34_out, and_35_out, not_1_out, not_2_out, not_3_out, not_4_out, not_5_out, not_6_out, not_7_out,
       not_8_out, not_9_out, not_10_out, not_11_out, not_12_out, not_13_out, not_14_out, not_15_out,
       not_16_out, not_17_out, not_18_out, not_19_out, not_20_out, not_21_out, not_22_out, not_23_out,
       not_24_out, not_25_out, not_26_out, not_27_out, not_28_out, not_29_out, not_30_out, not_31_out,
       not_32_out, not_33_out, not_34_out, not_35_out, not_36_out, not_37_out, not_38_out, not_39_out,
       not_40_out, not_41_out, not_42_out, not_43_out, not_44_out, not_45_out, not_46_out, not_47_out,
       not_48_out, not_49_out, not_50_out, not_51_out, not_52_out, not_53_out, not_54_out;

  not not_1 (not_1_out, S0);
  not not_2 (not_2_out, S1);
  not not_3 (not_3_out, S0);
  not not_4 (not_4_out, S2);
  not not_5 (not_5_out, S3);
  not not_6 (not_6_out, S4);
  not not_7 (not_7_out, S1);
  not not_8 (not_8_out, S2);
  not not_9 (not_9_out, S2);
  not not_10 (not_10_out, S3);
  not not_11 (not_11_out, S1);
  not not_12 (not_12_out, S2);
  not not_13 (not_13_out, S1);
  not not_14 (not_14_out, S3);
  not not_15 (not_15_out, S4);
  not not_16 (not_16_out, S0);
  not not_17 (not_17_out, S3);
  not not_18 (not_18_out, S4);
  not not_19 (not_19_out, S0);
  not not_20 (not_20_out, S2);
  not not_21 (not_21_out, S3);
  not not_22 (not_22_out, S0);
  not not_23 (not_23_out, S2);
  not not_24 (not_24_out, S2);
  not not_25 (not_25_out, S3);
  not not_26 (not_26_out, S1);
  not not_27 (not_27_out, S4);
  not not_28 (not_28_out, S2);
  not not_29 (not_29_out, S3);
  not not_30 (not_30_out, S1);
  not not_31 (not_31_out, S4);
  not not_32 (not_32_out, S4);
  not not_33 (not_33_out, S3);
  not not_34 (not_34_out, S4);
  not not_35 (not_35_out, S0);
  not not_36 (not_36_out, S2);
  not not_37 (not_37_out, S3);
  not not_38 (not_38_out, S4);
  not not_39 (not_39_out, S1);
  not not_40 (not_40_out, S1);
  not not_41 (not_41_out, S3);
  not not_42 (not_42_out, S4);
  not not_43 (not_43_out, S2);
  not not_44 (not_44_out, S0);
  not not_45 (not_45_out, S2);
  not not_46 (not_46_out, S2);
  not not_47 (not_47_out, S4);
  not not_48 (not_48_out, S0);
  not not_49 (not_49_out, S1);
  not not_50 (not_50_out, S3);
  not not_51 (not_51_out, S4);
  not not_52 (not_52_out, S2);
  not not_53 (not_53_out, S3);
  not not_54 (not_54_out, S3);
  and and_1 (and_1_out, not_1_out, not_2_out, S2);
  and and_2 (and_2_out, not_3_out, S1, not_4_out, not_5_out);
  and and_3 (and_3_out, S1, S3, not_6_out);
  and and_4 (and_4_out, S0, not_7_out, not_8_out);
  and and_5 (and_5_out, S0, not_9_out, S3);
  and and_6 (and_6_out, S0, S2, not_10_out);
  and and_7 (and_7_out, not_11_out, not_12_out, S3);
  and and_8 (and_8_out, not_13_out, S3, S4);
  and and_9 (and_9_out, S1, not_14_out, not_15_out);
  and and_10 (and_10_out, not_16_out, S1, S4);
  and and_11 (and_11_out, S1, S2, not_17_out);
  and and_12 (and_12_out, S0, S2, not_18_out);
  and and_13 (and_13_out, not_19_out, not_20_out, not_21_out);
  and and_14 (and_14_out, not_22_out, not_23_out, S4);
  and and_15 (and_15_out, not_24_out, not_25_out, S4);
  and and_16 (and_16_out, not_26_out, S2, S3, not_27_out);
  and and_17 (and_17_out, S1, not_28_out, S4);
  and and_18 (and_18_out, S1, not_29_out, S4);
  and and_19 (and_19_out, S0, not_30_out, S2, not_31_out);
  and and_20 (and_20_out, S0, S2, S3, not_32_out);
  and and_21 (and_21_out, S1, S2, not_33_out, S4);
  and and_22 (and_22_out, S1, S2, S3, not_34_out);
  and and_23 (and_23_out, not_35_out, not_36_out, not_37_out, not_38_out);
  and and_24 (and_24_out, not_39_out, S2, S4);
  and and_25 (and_25_out, not_40_out, S2, S3);
  and and_26 (and_26_out, S1, not_41_out, not_42_out);
  and and_27 (and_27_out, S1, not_43_out, S3);
  and and_28 (and_28_out, S1, S3, S4);
  and and_29 (and_29_out, S0, S1);
  and and_30 (and_30_out, not_44_out, not_45_out, S4);
  and and_31 (and_31_out, not_46_out, S3, not_47_out);
  and and_32 (and_32_out, not_48_out, not_49_out, S2, not_50_out, not_51_out);
  and and_33 (and_33_out, S1, S3, S4);
  and and_34 (and_34_out, S0, not_52_out, not_53_out);
  and and_35 (and_35_out, S0, S1, not_54_out);
  or or_1 (A1, and_1_out, and_2_out, and_3_out, and_4_out, and_5_out, and_6_out);
  or or_2 (A2, and_7_out, and_8_out, and_9_out, and_10_out, and_11_out, and_12_out);
  or or_3 (A3, and_13_out, and_14_out, and_15_out, and_16_out, and_17_out, and_18_out, and_19_out, and_20_out);
  or or_4 (B1, and_21_out, and_22_out, S0);
  or or_5 (B2, and_23_out, and_24_out, and_25_out, and_26_out, and_27_out, and_28_out, and_29_out);
  or or_6 (B3, and_30_out, and_31_out, and_32_out, and_33_out, and_34_out, and_35_out);
endmodule

module Mejor_movimiento (
  input  A,
  input  B,
  input  C,
  input  D,
  input  E,
  output A1,
  output B1,
  output C1,
  output D1,
  output E1
);

  wire and_1_out, and_2_out, and_3_out, and_4_out, and_5_out, and_6_out, and_7_out, and_8_out, and_9_out,
       and_10_out, and_11_out, and_12_out, and_13_out, and_14_out, and_15_out, and_16_out, and_17_out,
       and_18_out, and_19_out, and_20_out, and_21_out, and_22_out, and_23_out, and_24_out, and_25_out,
       and_26_out, and_27_out, and_28_out, and_29_out, not_1_out, not_2_out, not_3_out, not_4_out, not_5_out,
       not_6_out, not_7_out, not_8_out, not_9_out, not_10_out, not_11_out, not_12_out, not_13_out,
       not_14_out, not_15_out, not_16_out, not_17_out, not_18_out, not_19_out, not_20_out, not_21_out,
       not_22_out, not_23_out, not_24_out, not_25_out, not_26_out, not_27_out, not_28_out, not_29_out,
       not_30_out, not_31_out, not_32_out, not_33_out, not_34_out, not_35_out, not_36_out, not_37_out,
       not_38_out, not_39_out, not_40_out, not_41_out, not_42_out, not_43_out, not_44_out, not_45_out,
       not_46_out, not_47_out, not_48_out;

  not not_1 (not_1_out, E);
  not not_2 (not_2_out, B);
  not not_3 (not_3_out, C);
  not not_4 (not_4_out, D);
  not not_5 (not_5_out, A);
  not not_6 (not_6_out, D);
  not not_7 (not_7_out, A);
  not not_8 (not_8_out, C);
  not not_9 (not_9_out, A);
  not not_10 (not_10_out, C);
  not not_11 (not_11_out, D);
  not not_12 (not_12_out, E);
  not not_13 (not_13_out, A);
  not not_14 (not_14_out, B);
  not not_15 (not_15_out, B);
  not not_16 (not_16_out, E);
  not not_17 (not_17_out, A);
  not not_18 (not_18_out, D);
  not not_19 (not_19_out, E);
  not not_20 (not_20_out, D);
  not not_21 (not_21_out, C);
  not not_22 (not_22_out, E);
  not not_23 (not_23_out, E);
  not not_24 (not_24_out, B);
  not not_25 (not_25_out, C);
  not not_26 (not_26_out, D);
  not not_27 (not_27_out, B);
  not not_28 (not_28_out, C);
  not not_29 (not_29_out, E);
  not not_30 (not_30_out, A);
  not not_31 (not_31_out, D);
  not not_32 (not_32_out, B);
  not not_33 (not_33_out, A);
  not not_34 (not_34_out, C);
  not not_35 (not_35_out, E);
  not not_36 (not_36_out, D);
  not not_37 (not_37_out, E);
  not not_38 (not_38_out, C);
  not not_39 (not_39_out, A);
  not not_40 (not_40_out, B);
  not not_41 (not_41_out, E);
  not not_42 (not_42_out, C);
  not not_43 (not_43_out, E);
  not not_44 (not_44_out, D);
  not not_45 (not_45_out, E);
  not not_46 (not_46_out, A);
  not not_47 (not_47_out, C);
  not not_48 (not_48_out, E);
  and and_1 (and_1_out, B, C, D, not_1_out);
  and and_2 (and_2_out, A, not_2_out);
  and and_3 (and_3_out, A, not_3_out);
  and and_4 (and_4_out, A, not_4_out);
  and and_5 (and_5_out, not_5_out, C, not_6_out, E);
  and and_6 (and_6_out, not_7_out, B, E);
  and and_7 (and_7_out, B, not_8_out, E);
  and and_8 (and_8_out, not_9_out, B, not_10_out, D);
  and and_9 (and_9_out, B, C, not_11_out);
  and and_10 (and_10_out, A, B, C, not_12_out);
  and and_11 (and_11_out, not_13_out, D, E);
  and and_12 (and_12_out, not_14_out, D, E);
  and and_13 (and_13_out, not_15_out, C, not_16_out);
  and and_14 (and_14_out, not_17_out, B, not_18_out, not_19_out);
  and and_15 (and_15_out, B, C, not_20_out, E);
  and and_16 (and_16_out, A, B, not_21_out, not_22_out);
  and and_17 (and_17_out, A, B, D, not_23_out);
  and and_18 (and_18_out, not_24_out, not_25_out, not_26_out, E);
  and and_19 (and_19_out, not_27_out, not_28_out, D, not_29_out);
  and and_20 (and_20_out, not_30_out, C, not_31_out, E);
  and and_21 (and_21_out, not_32_out, C, D, E);
  and and_22 (and_22_out, not_33_out, B, not_34_out, not_35_out);
  and and_23 (and_23_out, A, B, not_36_out, not_37_out);
  and and_24 (and_24_out, A, B, not_38_out, D, E);
  and and_25 (and_25_out, not_39_out, not_40_out, not_41_out);
  and and_26 (and_26_out, not_42_out, not_43_out);
  and and_27 (and_27_out, B, not_44_out, not_45_out);
  and and_28 (and_28_out, not_46_out, B, not_47_out, D);
  and and_29 (and_29_out, A, D, not_48_out);
  or or_1 (A1, and_1_out, and_2_out, and_3_out, and_4_out);
  or or_2 (B1, and_5_out, and_6_out, and_7_out, and_8_out, and_9_out, and_10_out);
  or or_3 (C1, and_11_out, and_12_out, and_13_out, and_14_out, and_15_out, and_16_out, and_17_out);
  or or_4 (D1, and_18_out, and_19_out, and_20_out, and_21_out, and_22_out, and_23_out, and_24_out);
  or or_5 (E1, and_25_out, and_26_out, and_27_out, and_28_out, and_29_out);
endmodule

module FlipFlop_D (
  input  CLK,
  input  D,
  input  RESET,
  output A,
  output NOT_A
);

  wire nand_1_out, nand_2_out, nand_3_out, nand_4_out;

  nand nand_1 (nand_1_out, nand_4_out, nand_2_out);
  nand nand_2 (nand_2_out, nand_1_out, CLK, RESET);
  nand nand_3 (nand_3_out, nand_2_out, CLK, nand_4_out);
  nand nand_4 (nand_4_out, nand_3_out, D, RESET);
  nand nand_5 (A, nand_2_out, NOT_A);
  nand nand_6 (NOT_A, A, nand_3_out, RESET);
endmodule
